# Fritzing sketch Heltec LoRa-32-v2_BME680  (saved by Fritzing 0.9.4)
breadboards: 1

parts:
  Part1 = Adafruit BME680
  Heltec_WiFi_LoRa_32_V1 = Heltec WiFi LoRa 32 V2 [part_number=HTIT-WB32LA]

nets:
  N1: Part1.3.3V, Heltec_WiFi_LoRa_32_V1.pin_16, Heltec_WiFi_LoRa_32_V1.pin_17
  N2: Part1.GND, Heltec_WiFi_LoRa_32_V1.pin_18, Heltec_WiFi_LoRa_32_V1.pin_19
  N3: Part1.SCK/SCL, Heltec_WiFi_LoRa_32_V1.pin_32
  N4: Part1.SDI/SDA, Heltec_WiFi_LoRa_32_V1.pin_34
  N5: Heltec_WiFi_LoRa_32_V1.pin_21, Heltec_WiFi_LoRa_32_V1.pin_22

custom parts:
  Heltec WiFi LoRa 32 V2: Heltec WiFi LoRa 32 V2 WiFi LoRa 32 is a classic IoT dev-board designed & produced by Heltec Automation(TM). It’s a highly integrated product based on ESP32 + SX127x, it has Wi-Fi, BLE, LoRa functions, also Li-Po battery management system, 0.96″ OLED are also included. It’s the best choice for smart cities, smart farms, smart home, and IoT makers.
